# Fritzing sketch Ski Sensor Module (saved by Fritzing 0.9.3b)
circuit board: 8.46667cm x 5.64444cm
breadboards: 1

parts:
  Part1 = Arduino Nano (Rev3.0) (ICSP)
  GY-NEO6MV3 = SUP500F [package=sup500f]
  BAT1 = Battery Holders [package=lipo-1100mAh]
  T1 = NodeMCU V3.0
  T2 = NodeMCU V3.0
  Part2 = MicroSD Card Module
  J1 = Piezo Speaker
  J2 = Piezo Speaker
  J3 = Piezo Speaker
  J4 = Piezo Speaker
  J5 = Piezo Speaker
  U1 = TMP36 [package=to-92]

nets:
  N1: Part1.D0/RX, T1.TX, T2.TX
  N2: Part1.D9, GY-NEO6MV3.TX-O
  N3: Part1.D10, Part2.CS
  N4: Part1.D11/MOSI, Part2.MOSI
  N5: Part1.D12/MISO, Part2.MISO
  VIN: Part1.VIN, GY-NEO6MV3.VCC, BAT1.+, T1.Vin, T2.Vin, U1.VCC
  GND: Part1.GND, GY-NEO6MV3.GND, BAT1.-, T1.GND, T2.GND, J1.pin1, J2.pin1, J3.pin1, J4.pin1, J5.pin1, U1.GND
  N6: Part1.A5, U1.VOUT
  N7: Part1.A4, J5.pin2
  N8: Part1.A3, J3.pin2
  N9: Part1.A2, J4.pin2
  N10: Part1.A1, J2.pin2
  N11: Part1.A0, J1.pin2
  N12: Part1.D13/SCK, Part2.SCK

custom parts:
  NodeMCU V3.0: ESP8266 based NodeMCU
